// Logisim project control_logic.circ as structural Verilog: 1 circuit, main circuit control_logic
module control_logic (
  input  [31:0] inst,
  input  BrEq,
  input  BrLt,
  output PCSel,
  output RegWEn,
  output [2:0] ImmSel,
  output BrUn,
  output ASel,
  output BSel,
  output [3:0] ALUSel,
  output MemRW,
  output [1:0] WBSel,
  output CSRSel,
  output CSRWen,
  output is_lui
);

  wire and_1_out, and_2_out, and_3_out, and_4_out, and_5_out, and_6_out, and_7_out, BrGe, BrNe,
       comparator_1_eq, comparator_2_eq, comparator_3_eq, comparator_4_eq, comparator_5_eq, comparator_6_eq,
       comparator_7_eq, comparator_8_eq, comparator_9_eq, comparator_11_eq, comparator_12_eq,
       comparator_13_eq, comparator_14_eq, comparator_15_eq, comparator_16_eq, comparator_18_eq,
       comparator_19_eq, comparator_20_eq, comparator_21_eq, comparator_22_eq, comparator_23_eq,
       comparator_24_eq, comparator_25_eq, comparator_27_eq, comparator_28_eq, comparator_29_eq,
       comparator_30_eq, comparator_31_eq, comparator_32_eq, comparator_33_eq, comparator_34_eq,
       comparator_35_eq, comparator_36_eq, comparator_37_eq, comparator_38_eq, comparator_39_eq,
       comparator_40_eq, comparator_41_eq, comparator_42_eq, comparator_43_eq, comparator_44_eq,
       comparator_45_eq, comparator_46_eq, comparator_47_eq, comparator_48_eq, comparator_49_eq,
       comparator_50_eq, comparator_51_eq, comparator_52_eq, comparator_53_eq, comparator_54_eq,
       comparator_55_eq, isMul, isMulh, isSra, isSub, Mem, nor_1_out, or_1_out, or_3_out, or_7_out, or_8_out,
       or_9_out, or_10_out, or_11_out, PC_add4, priority_encoder_1_gs, RegWEn_alternative;
  wire [3:0] multiplexer_1_out, multiplexer_2_out, multiplexer_3_out, multiplexer_4_out, RIsel;

  Comparator #(.width(3)) comparator_1 (.a(3'b000), .b(inst[14:12]), .eq(comparator_1_eq));  // open: gt, lt
  Comparator #(.width(3)) comparator_2 (.a(3'b001), .b(inst[14:12]), .eq(comparator_2_eq));  // open: gt, lt
  Comparator #(.width(3)) comparator_3 (.a(3'b100), .b(inst[14:12]), .eq(comparator_3_eq));  // open: gt, lt
  Comparator #(.width(3)) comparator_4 (.a(3'b101), .b(inst[14:12]), .eq(comparator_4_eq));  // open: gt, lt
  Comparator #(.width(3)) comparator_5 (.a(3'b110), .b(inst[14:12]), .eq(comparator_5_eq));  // open: gt, lt
  Comparator #(.width(3)) comparator_6 (.a(3'b111), .b(inst[14:12]), .eq(comparator_6_eq));  // open: gt, lt
  Comparator #(.width(7)) comparator_7 (.a(7'b1100011), .b(inst[6:0]), .eq(comparator_7_eq));  // open: gt, lt
  Comparator #(.width(7)) comparator_8 (.a(7'b1101111), .b(inst[6:0]), .eq(comparator_8_eq));  // open: gt, lt
  Comparator #(.width(7)) comparator_9 (.a(7'b0010111), .b(inst[6:0]), .eq(comparator_9_eq));  // open: gt, lt
  Comparator #(.width(7)) comparator_10 (.a(7'b0000011), .b(inst[6:0]), .eq(Mem));  // open: gt, lt
  Comparator #(.width(7)) comparator_11 (.a(7'b1101111), .b(inst[6:0]), .eq(comparator_11_eq));  // open: gt, lt
  Comparator #(.width(7)) comparator_12 (.a(7'b1100111), .b(inst[6:0]), .eq(comparator_12_eq));  // open: gt, lt
  not not_1 (BrNe, BrEq);
  or or_1 (or_1_out, BrEq, BrLt);
  and and_1 (and_1_out, BrEq, comparator_1_eq);
  and and_2 (and_2_out, BrNe, comparator_2_eq);
  and and_3 (and_3_out, BrLt, comparator_3_eq);
  and and_4 (and_4_out, BrGe, comparator_4_eq);
  and and_5 (and_5_out, BrLt, comparator_5_eq);
  and and_6 (and_6_out, BrGe, comparator_6_eq);
  or or_2 (ASel, comparator_7_eq, comparator_8_eq, comparator_9_eq);
  not not_2 (BrGe, or_1_out);
  Comparator #(.width(7)) comparator_13 (.a(7'b1100011), .b(inst[6:0]), .eq(comparator_13_eq));  // open: gt, lt
  or or_3 (or_3_out, and_1_out, and_2_out, and_3_out, and_4_out, and_5_out, and_6_out);
  nor nor_1 (nor_1_out, Mem, PC_add4);
  or or_4 (PC_add4, comparator_11_eq, comparator_12_eq);
  or or_5 (PCSel, and_7_out, comparator_14_eq, comparator_15_eq);
  and and_7 (and_7_out, comparator_13_eq, or_3_out);
  Comparator #(.width(7)) comparator_14 (.a(7'b1100111), .b(inst[6:0]), .eq(comparator_14_eq));  // open: gt, lt
  Comparator #(.width(7)) comparator_15 (.a(7'b1101111), .b(inst[6:0]), .eq(comparator_15_eq));  // open: gt, lt
  Priority_Encoder #(.select(2)) priority_encoder_1 (
    .in0(Mem), .in1(nor_1_out), .in2(PC_add4), .out(WBSel), .gs(priority_encoder_1_gs), .en_in(1'b1));  // open: in3, en_out
  Comparator #(.width(7)) comparator_16 (.a(7'b0110011), .b(inst[6:0]), .eq(comparator_16_eq));  // open: gt, lt
  Comparator #(.width(7)) comparator_17 (.a(7'b0110111), .b(inst[6:0]), .eq(is_lui));  // open: gt, lt
  not not_3 (BSel, comparator_16_eq);
  or or_6 (RegWEn, comparator_18_eq, comparator_19_eq, comparator_20_eq, comparator_21_eq, comparator_22_eq, comparator_23_eq, comparator_24_eq);
  Comparator #(.width(7)) comparator_18 (.a(7'b0110011), .b(inst[6:0]), .eq(comparator_18_eq));  // open: gt, lt
  Comparator #(.width(7)) comparator_19 (.a(7'b0000011), .b(inst[6:0]), .eq(comparator_19_eq));  // open: gt, lt
  Comparator #(.width(7)) comparator_20 (.a(7'b0010011), .b(inst[6:0]), .eq(comparator_20_eq));  // open: gt, lt
  Comparator #(.width(7)) comparator_21 (.a(7'b0010111), .b(inst[6:0]), .eq(comparator_21_eq));  // open: gt, lt
  Comparator #(.width(7)) comparator_22 (.a(7'b0110111), .b(inst[6:0]), .eq(comparator_22_eq));  // open: gt, lt
  Comparator #(.width(7)) comparator_23 (.a(7'b1101111), .b(inst[6:0]), .eq(comparator_23_eq));  // open: gt, lt
  Comparator #(.width(7)) comparator_24 (.a(7'b1100111), .b(inst[6:0]), .eq(comparator_24_eq));  // open: gt, lt
  Comparator #(.width(3)) comparator_25 (.a(3'b101), .b(inst[14:12]), .eq(comparator_25_eq));  // open: gt, lt
  Comparator #(.width(7)) comparator_26 (.a(7'b0100011), .b(inst[6:0]), .eq(MemRW));  // open: gt, lt
  and and_8 (CSRSel, CSRWen, comparator_25_eq);
  Comparator #(.width(7)) comparator_27 (.a(7'b0000011), .b(inst[6:0]), .eq(comparator_27_eq));  // open: gt, lt
  Comparator #(.width(7)) comparator_28 (.a(7'b0010011), .b(inst[6:0]), .eq(comparator_28_eq));  // open: gt, lt
  Comparator #(.width(7)) comparator_29 (.a(7'b0100011), .b(inst[6:0]), .eq(comparator_29_eq));  // open: gt, lt
  Comparator #(.width(7)) comparator_30 (.a(7'b1100011), .b(inst[6:0]), .eq(comparator_30_eq));  // open: gt, lt
  Comparator #(.width(7)) comparator_31 (.a(7'b0010111), .b(inst[6:0]), .eq(comparator_31_eq));  // open: gt, lt
  Comparator #(.width(7)) comparator_32 (.a(7'b0110111), .b(inst[6:0]), .eq(comparator_32_eq));  // open: gt, lt
  Comparator #(.width(7)) comparator_33 (.a(7'b1101111), .b(inst[6:0]), .eq(comparator_33_eq));  // open: gt, lt
  Comparator #(.width(7)) comparator_34 (.a(7'b1110011), .b(inst[6:0]), .eq(comparator_34_eq));  // open: gt, lt
  Comparator #(.width(3)) comparator_35 (.a(3'b001), .b(inst[14:12]), .eq(comparator_35_eq));  // open: gt, lt
  Comparator #(.width(3)) comparator_36 (.a(3'b101), .b(inst[14:12]), .eq(comparator_36_eq));  // open: gt, lt
  or or_7 (or_7_out, comparator_27_eq, comparator_28_eq);
  or or_8 (or_8_out, comparator_31_eq, comparator_32_eq);
  nor nor_2 (RegWEn_alternative, comparator_37_eq, comparator_38_eq);
  Comparator #(.width(7)) comparator_37 (.a(7'b0100011), .b(inst[6:0]), .eq(comparator_37_eq));  // open: gt, lt
  Comparator #(.width(7)) comparator_38 (.a(7'b1100011), .b(inst[6:0]), .eq(comparator_38_eq));  // open: gt, lt
  Comparator #(.width(7)) comparator_39 (.a(7'b1110011), .b(inst[6:0]), .eq(comparator_39_eq));  // open: gt, lt
  and and_9 (CSRWen, comparator_39_eq, or_9_out);
  or or_9 (or_9_out, comparator_35_eq, comparator_36_eq);
  Priority_Encoder priority_encoder_2 (
    .in0(or_7_out), .in1(comparator_29_eq), .in2(comparator_30_eq), .in3(or_8_out), .in4(comparator_33_eq),
    .in5(comparator_34_eq), .out(ImmSel), .en_in(1'b1));  // open: in6, in7, gs, en_out
  Multiplexer #(.enable("false"), .select(3), .width(4)) multiplexer_1 (
    .in0(4'b0000), .in1(4'b0110), .in2(4'b0111), .in3(4'b1011), .in4(4'b0011), .in5(4'b0100), .in6(4'b0010),
    .in7(4'b0001), .out(multiplexer_1_out), .sel(inst[14:12]));
  Multiplexer #(.enable("false"), .width(4)) multiplexer_2 (
    .in0(multiplexer_1_out), .in1(4'b1010), .out(multiplexer_2_out), .sel(isMul));
  Comparator #(.width(7)) comparator_40 (.a(inst[31:25]), .b(7'b0000001), .eq(comparator_40_eq));  // open: gt, lt
  Comparator #(.width(3)) comparator_41 (.a(inst[14:12]), .b(3'b000), .eq(comparator_41_eq));  // open: gt, lt
  Comparator #(.width(7)) comparator_42 (.a(inst[6:0]), .b(7'b0110011), .eq(comparator_42_eq));  // open: gt, lt
  Comparator #(.width(7)) comparator_43 (.a(inst[31:25]), .b(7'b0100000), .eq(comparator_43_eq));  // open: gt, lt
  Comparator #(.width(3)) comparator_44 (.a(inst[14:12]), .b(3'b000), .eq(comparator_44_eq));  // open: gt, lt
  Comparator #(.width(7)) comparator_45 (.a(inst[6:0]), .b(7'b0110011), .eq(comparator_45_eq));  // open: gt, lt
  Comparator #(.width(7)) comparator_46 (.a(inst[31:25]), .b(7'b0000001), .eq(comparator_46_eq));  // open: gt, lt
  Comparator #(.width(3)) comparator_47 (.a(inst[14:12]), .b(3'b001), .eq(comparator_47_eq));  // open: gt, lt
  Comparator #(.width(7)) comparator_48 (.a(inst[6:0]), .b(7'b0110011), .eq(comparator_48_eq));  // open: gt, lt
  Comparator #(.width(7)) comparator_49 (.a(inst[31:25]), .b(7'b0100000), .eq(comparator_49_eq));  // open: gt, lt
  Comparator #(.width(3)) comparator_50 (.a(inst[14:12]), .b(3'b101), .eq(comparator_50_eq));  // open: gt, lt
  Comparator #(.width(3)) comparator_51 (.a(3'b110), .b(inst[14:12]), .eq(comparator_51_eq));  // open: gt, lt
  Comparator #(.width(3)) comparator_52 (.a(3'b111), .b(inst[14:12]), .eq(comparator_52_eq));  // open: gt, lt
  Multiplexer #(.enable("false"), .width(4)) multiplexer_3 (
    .in0(multiplexer_2_out), .in1(4'b1100), .out(multiplexer_3_out), .sel(isSub));
  and and_10 (isMul, comparator_40_eq, comparator_41_eq, comparator_42_eq);
  and and_11 (isSub, comparator_43_eq, comparator_44_eq, comparator_45_eq);
  and and_12 (isMulh, comparator_46_eq, comparator_47_eq, comparator_48_eq);
  and and_13 (isSra, comparator_49_eq, comparator_50_eq);
  Comparator #(.width(7)) comparator_53 (.a(7'b1100011), .b(inst[6:0]), .eq(comparator_53_eq));  // open: gt, lt
  or or_10 (or_10_out, comparator_51_eq, comparator_52_eq);
  Multiplexer #(.enable("false"), .width(4)) multiplexer_4 (
    .in0(multiplexer_3_out), .in1(4'b1110), .out(multiplexer_4_out), .sel(isMulh));
  and and_14 (BrUn, comparator_53_eq, or_10_out);
  Multiplexer #(.enable("false"), .width(4)) multiplexer_5 (
    .in0(multiplexer_4_out), .in1(4'b0101), .out(RIsel), .sel(isSra));
  Comparator #(.width(7)) comparator_54 (.a(inst[6:0]), .b(7'b0110011), .eq(comparator_54_eq));  // open: gt, lt
  Comparator #(.width(7)) comparator_55 (.a(inst[6:0]), .b(7'b0010011), .eq(comparator_55_eq));  // open: gt, lt
  Multiplexer #(.enable("false"), .width(4)) multiplexer_6 (.in0(4'b0000), .in1(RIsel), .out(ALUSel), .sel(or_11_out));
  or or_11 (or_11_out, comparator_54_eq, comparator_55_eq);

  // Other names for the same wires on the sheet: Opcode[6:0] = inst[6:0]; Funct3[2:0] = inst[14:12];
  //   Funct7[6:0] = inst[31:25]

  // Notes on the sheet:
  //   INPUTS to your circuit
  //   SB
  //   UJ
  //   auipc_lui
  //   DON'T CHANGE THE LOCATIONS OF THE INPUTS AND OUTPUTS!
  //   OUTPUT from your circuit
  //   SW
  //   SB
  //   I-imm
  //   S-imm
  //   SB-imm
  //   U-imm
  //   UJ-imm
  //   csrw-imm
  //   ALU 逻辑，由于部分R指令和I指令共用同一个ALUsel，因此特判了mulh等R独有的指令
  //   R-instr
  //   I-instr
  //   除了R和I型计算指令，其余都默认加法
endmodule
