// Logisim project cpu.circ as structural Verilog: 1 circuit, main circuit cpu
module cpu (
  input  clk,
  input  [31:0] INSTRUCTION,
  input  [31:0] READ_DATA,
  output [31:0] WRITE_ADDRESS,
  output [31:0] PROGRAM_COUNTER,
  output [31:0] ra,
  output [31:0] sp,
  output [31:0] t0,
  output [31:0] t1,
  output [31:0] t2,
  output [31:0] s0,
  output [31:0] s1,
  output [31:0] a0,
  output [31:0] tohost,
  output [3:0] WRITE_ENABLE,
  output [31:0] WRITE_DATA
);

  wire ASel, BrEq, BrLt, BrUn, BSel, CSRSel, CSRWen, is_lui, MemRW, PCSel, RegWEn;
  wire [1:0] WBSel;
  wire [2:0] func3, ImmSel;
  wire [3:0] ALUSel, bit_extender_1_out, multiplexer_4_out;
  wire [4:0] rs1;
  wire [16:0] bit_extender_3_out;
  wire [24:0] bit_extender_2_out;
  wire [31:0] adder_1_out, Data_aligned, DataD, Imm, Inst_d, Inst_IF, multiplexer_1_out, multiplexer_5_out,
       multiplexer_6_out, multiplexer_7_out, PC_add4, PC_d, Read_Data1;

  Adder #(.width(32)) adder_1 (.a(PROGRAM_COUNTER), .b(32'h4), .out(adder_1_out));  // open: cin, cout
  Multiplexer #(.enable("false"), .width(32)) multiplexer_1 (
    .in0(adder_1_out), .in1(WRITE_ADDRESS), .out(multiplexer_1_out), .sel(PCSel));
  Register #(.width(32)) register_1 (.D(PROGRAM_COUNTER), .en(1'b1), .clk(clk), .Q(PC_d));  // open: clr
  Register #(.width(32)) PC (.D(multiplexer_1_out), .en(1'b1), .clk(clk), .Q(PROGRAM_COUNTER));  // open: clr
  Register #(.width(32)) register_2 (
    .D(Inst_IF), .en(1'b1), .clk(clk), .Q({Inst_d[31:15], func3, Inst_d[11:0]}));  // open: clr
  Multiplexer #(.enable("false"), .width(32)) multiplexer_2 (
    .in0(INSTRUCTION), .in1(32'h13), .out(Inst_IF), .sel(PCSel));
  imm_gen imm_gen_1 (.inst({Inst_d[31:15], func3, Inst_d[11:0]}), .ImmSel(ImmSel), .imm(Imm));
  Multiplexer #(.enable("false"), .width(5)) multiplexer_3 (
    .in0(Inst_d[19:15]), .in1({5{1'b0}}), .out(rs1), .sel(is_lui));
  control_logic control_logic_1 (
    .CSRWen(CSRWen), .is_lui(is_lui), .PCSel(PCSel), .RegWEn(RegWEn), .ImmSel(ImmSel), .BrUn(BrUn),
    .ASel(ASel), .BSel(BSel), .ALUSel(ALUSel), .MemRW(MemRW), .WBSel(WBSel), .CSRSel(CSRSel),
    .inst({Inst_d[31:15], func3, Inst_d[11:0]}), .BrEq(BrEq), .BrLt(BrLt));
  assign bit_extender_1_out = {{3{MemRW}}, MemRW};  // Bit_Extender bit_extender_1
  Multiplexer #(.enable("false"), .select(3), .width(4)) multiplexer_4 (
    .in0(4'b0001), .in1(4'b0011), .in2(4'b1111), .in3(4'b0000), .in4(4'b0000), .in5(4'b0000), .in6(4'b0000),
    .in7(4'b0000), .out(multiplexer_4_out), .sel(func3));
  regfile regfile_1 (
    .rs1(rs1), .rs2(Inst_d[24:20]), .rd(Inst_d[11:7]), .Write_Data(DataD), .RegWEn(RegWEn), .clk(clk),
    .ra(ra), .sp(sp), .t0(t0), .t1(t1), .t2(t2), .s0(s0), .s1(s1), .a0(a0), .Read_Data_1(Read_Data1),
    .Read_Data_2(WRITE_DATA));
  branch_comp branch_comp_1 (.rs1(Read_Data1), .rs2(WRITE_DATA), .BrUn(BrUn), .BrEq(BrEq), .BrLt(BrLt));
  assign WRITE_ENABLE = bit_extender_1_out & multiplexer_4_out;  // AND_Gate and_1, 4 bits wide
  Multiplexer #(.enable("false"), .width(32)) multiplexer_5 (
    .in0(Read_Data1), .in1(PC_d), .out(multiplexer_5_out), .sel(ASel));
  Multiplexer #(.enable("false"), .width(32)) multiplexer_6 (
    .in0(WRITE_DATA), .in1(Imm), .out(multiplexer_6_out), .sel(BSel));
  Multiplexer #(.enable("false"), .width(32)) multiplexer_7 (
    .in0(Read_Data1), .in1(Imm), .out(multiplexer_7_out), .sel(CSRSel));
  assign bit_extender_2_out = {{24{READ_DATA[7]}}, READ_DATA[7]};  // Bit_Extender bit_extender_2
  assign bit_extender_3_out = {{16{READ_DATA[15]}}, READ_DATA[15]};  // Bit_Extender bit_extender_3
  alu alu_1 (.Result(WRITE_ADDRESS), .A(multiplexer_5_out), .B(multiplexer_6_out), .ALUSel(ALUSel));
  csr csr_1 (.CSR_address(12'h51e), .CSR_din(multiplexer_7_out), .CSR_WE(CSRWen), .clk(clk), .tohost(tohost));
  Adder #(.width(32)) adder_2 (.a(32'h4), .b(PC_d), .out(PC_add4));  // open: cin, cout
  Multiplexer #(.enable("false"), .select(2), .width(32)) multiplexer_8 (
    .in0(Data_aligned), .in1(WRITE_ADDRESS), .in2(PC_add4), .out(DataD), .sel(WBSel));  // open: in3
  Multiplexer #(.enable("false"), .select(3), .width(32)) multiplexer_9 (
    .in0({bit_extender_2_out, READ_DATA[6:0]}), .in1({bit_extender_3_out, READ_DATA[14:0]}), .in2(READ_DATA),
    .in3({32{1'b0}}), .in4({32{1'b0}}), .in5({32{1'b0}}), .in6({32{1'b0}}), .in7({32{1'b0}}),
    .out(Data_aligned), .sel(func3));

  // Other names for the same wires on the sheet: rd[4:0] = Inst_d[11:7]; Inst_d[14:12] = func3;
  //   rs1_inst[4:0] = Inst_d[19:15]; rs2[4:0] = Inst_d[24:20]; Read_Data2[31:0] = WRITE_DATA;
  //   Result[31:0] = WRITE_ADDRESS

  // Notes on the sheet:
  //   Output to IMEM
  //   IMEM (do **NOT** move this)
  //   Inputs from IMEM
  //   It is OK to move the PC, RegFile, ALU, MEM, Branch Comp, Imm Gen, and Control Logic to wherever is most convenient for you when constructing your CPU, and to delete this text
  //   Inputs/Outputs for testing. Do **NOT** move these.
  //   Outputs To DMEM
  //   DMEM (do **NOT** move this)
  //   Inputs From DMEM
endmodule
